// Logisim project dlat.circ as structural Verilog: 1 circuit, main circuit main
module main (
  input  RST,
  input  CLK,
  input  nIN,
  output OUT,
  output nOUT
);

  wire nor_1_out, nor_2_out, nor_3_out, nor_4_out;

  nor nor_1 (nor_1_out, nor_2_out, CLK, nor_3_out);
  nor nor_2 (nor_2_out, nor_1_out, RST, nIN);
  nor nor_3 (nor_3_out, CLK, RST, nor_4_out);
  nor nor_4 (nor_4_out, nor_3_out, nor_2_out);
  nor nor_5 (OUT, RST, nor_1_out, nOUT);
  nor nor_6 (nOUT, OUT, nor_3_out);
endmodule
