// Logisim project flip.circ as structural Verilog: 1 circuit, main circuit main
module main (
  input  REQ,
  output OUT
);

  wire nor_1_out, nor_2_out, nor_3_out, nor_4_out, nor_5_out, RCLK_out;

  Clock RCLK (.out(RCLK_out));
  nor nor_1 (nor_1_out, RCLK_out, REQ, nor_2_out);
  nor nor_2 (nor_2_out, nor_1_out, nor_4_out);
  nor nor_3 (nor_3_out, RCLK_out, nor_1_out, nor_4_out);
  nor nor_4 (nor_4_out, nor_3_out, REQ);
  nor nor_5 (nor_5_out, REQ, nor_3_out, OUT);
  nor nor_6 (OUT, nor_5_out, nor_1_out);
endmodule
