// Logisim project flipd.circ as structural Verilog: 1 circuit, main circuit main
module main (
  input  RES,
  input  DAT,
  output OUT,
  output OUT_2
);

  wire CLK_out, nor_1_out, nor_2_out, nor_3_out, nor_4_out;

  Clock CLK (.out(CLK_out));
  nor nor_1 (nor_1_out, RES, DAT, nor_2_out);
  nor nor_2 (nor_2_out, nor_1_out, CLK_out, nor_3_out);
  nor nor_3 (nor_3_out, RES, CLK_out, nor_4_out);
  nor nor_4 (nor_4_out, nor_3_out, nor_1_out);
  nor nor_5 (OUT, RES, nor_2_out, OUT_2);
  nor nor_6 (OUT_2, OUT, nor_3_out);
endmodule
